# Fritzing sketch neopixel_strip (saved by Fritzing 1.0.0rc)
breadboards: 1

parts:
  Part1 = Adafruit HUZZAH32 ESP32 Feather [part_number="Adafruit #3405"]
  NEOPIXEL1 = Neopixel Strip -- Black (30/m) [part_number=1376]
  R1 = Resistor [tolerance=±5% resistance=220 package="0805 [SMD]"]  # not connected

nets:
  N1: Part1.N/C, NEOPIXEL1.GND
  3.3V: Part1.3.3V, NEOPIXEL1.+5V

custom parts:
  Neopixel Strip -- Black (30/m): These NeoPixel strips have 30 digitally-addressable pixel LEDs per meter and are very affordable and are only 12.5 mm wide, 10 mm if you remove the strip from the casing.
