# Fritzing sketch photo_cell (saved by Fritzing 0.9.9b)
breadboards: 1

parts:
  R1 = Photocell (LDR) [package=THT]
  R2 = Resistor [tolerance=±5% power=0.25 resistance=2.2k package=THT]
  Part1 = Adafruit HUZZAH32 ESP32 Feather [part_number="Adafruit #3405"]

nets:
  N1: R1.pin_0, R2.Pin_1, Part1.A2_I34
  N2: R1.pin_1, Part1.3.3V
  N3: R2.Pin_0, Part1.GND
