# Fritzing sketch piezo (saved by Fritzing 1.0.0rc)
breadboards: 1

parts:
  Part1 = Adafruit HUZZAH32 ESP32 Feather [part_number="Adafruit #3405"]
  J1 = Piezo Speaker

nets:
  N1: Part1.GND, J1.pin1
  N2: Part1.IO27_A10, J1.pin2
