# Fritzing sketch range (saved by Fritzing 1.0.0rc)
breadboards: 1

parts:
  SONAR1 = Maxbotix MaxSonar Ultrasonic Sensor
  Part1 = Adafruit ESP32 Feather V2

nets:
  GND: SONAR1.GND, Part1.GND, Part1.SDA, Part1.IO27_A10
  +5V: SONAR1.+5V, Part1.3.3V
  N1: SONAR1.AN, Part1.A2_I34

custom parts:
  Maxbotix MaxSonar Ultrasonic Sensor: Maxbotix MaxSonar Ultrasonic Sensor LV-EZ0, LV-EZ1, LV-EZ2, LV-EZ3, LV-EZ4
